# Fritzing sketch Diagram (saved by Fritzing 0.8.7b)
breadboards: 1

parts:
  Part1 = Arduino Uno (Rev3)
  LED1 = LED - 5mm [color="Red (633nm)" package="5 mm [THT]"]
  R1 = Resistor [tolerance=±5% resistance=220 package=THT]
  R2 = Photocell (LDR) [package=THT]
  R3 = Resistor [tolerance=±5% resistance=220 package=THT]

nets:
  N1: Part1.A0, R2.pin_1, R3.Pin_0
  N2: Part1.D9_PWM, LED1.cathode
  N3: Part1.GND, R1.Pin_1, R3.Pin_1
  N4: Part1.5V, R2.pin_0
  N5: LED1.anode, R1.Pin_0

notes:
  330 Ohm
  10 KOhm
